# Fritzing sketch Schematic (saved by Fritzing 0.9.3b)

parts:
  Arduino_Uno = Arduino Uno (Rev3)
  Motor_Driver = L298N DC motor driver
  Barrel_Jack = Power Jack [package=power_jack_pth_lock]
  LCD = LCD1602-I2C
  DHT11_Temp_&_Humid_sensor = DHT11 basic temperature-humidity sensor [form="♂ (male)" package=THT]
  Fan = DC Motor

nets:
  N1: Arduino_Uno.A4/SDA, LCD.SDA
  N2: Arduino_Uno.A5/SCL, LCD.SCL
  N3: Arduino_Uno.D9_PWM, Motor_Driver.IN2
  N4: Arduino_Uno.D10_PWM/SS, Motor_Driver.IN1
  N5: Arduino_Uno.D11_PWM/MOSI, Motor_Driver.ENA
  GND: Arduino_Uno.GND, Motor_Driver.GND, Barrel_Jack.GND, LCD.GND, DHT11_Temp_&_Humid_sensor.GND
  N6: Arduino_Uno.D7, DHT11_Temp_&_Humid_sensor.OUT
  VCC: Arduino_Uno.5V, LCD.VCC, DHT11_Temp_&_Humid_sensor.VCC
  VIN: Arduino_Uno.VIN, Motor_Driver.5V, Motor_Driver.+5V-J1
  N7: Motor_Driver.OUT1, Fan.pin_1
  N8: Motor_Driver.OUT2, Fan.pin_2
  N9: Motor_Driver.12V, Barrel_Jack.PWR

notes:
  Automatic Air Cooling System

custom parts:
  L298N DC motor driver: 2x DC motor driver with 78M05 positive voltage regulator (7..35 V) L298N: max 46 V, 2 A Set 5 V Enable jumper to enable 5 V regultor (needed for the L298N) and +5 V output at screw terminal or supply external +5 V at screw terminal Set ENA and/or ENB to +5 V to enable motor permanently or supply ENA and/or ENB with PWM signal IN1 and IN2 set rotation directory for motor A (OUT1/OUT2) IN2 and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
  LCD1602-I2C: A standard character display, usually with 2x16 characters. Comes in many colors with LCM1602 IIC attached.
  DHT11 basic temperature-humidity sensor: The DHT11 is a basic, ultra low-cost digital temperature and humidity sensor. It uses a capacitive humidity sensor and a thermistor to measure the surrounding air, and spits out a digital signal on the data pin (no analog input pins needed). Its fairly simple to use, but requires careful timing to grab data. The only real downside of this sensor is you can only get new data from it once every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
